# Fritzing sketch circ11 (saved by Fritzing 0.9.3b)
breadboards: 1

parts:
  Part2 = Adafruit Metro with Headers [part_number="Adafruit #2488"]
  R1 = Relay 5v DPDT  # not connected
  D1 = Rectifier Diode [part_number=1N4001 package="300 mil [THT]"]
  R2 = Resistor [tolerance=±5% resistance=2.2k package=THT]
  LED1 = LED - 5mm [color="Green (565nm)" package="5 mm [THT]"]
  LED2 = LED - 5mm [color="Red (633nm)" package="5 mm [THT]"]
  R3 = Resistor [tolerance=±5% resistance=560 package=THT]
  R4 = Resistor [tolerance=±5% resistance=560 package=THT]
  Q2 = NPN-Transistor [package="TO92 [THT]"]

nets:
  N1: Part2.GND, D1.cathode, R3.Pin_1, R4.Pin_1, Q2.C
  N2: Part2.IO2, R2.Pin_1
  N3: D1.anode, Q2.E
  N4: R2.Pin_0, Q2.B
  N5: LED1.cathode, R3.Pin_0
  N6: LED2.cathode, R4.Pin_0

custom parts:
  Adafruit Metro with Headers: We sure love the ATmega328 here at Adafruit, and we use them a lot for our own projects. The processor has plenty of GPIO, Analog inputs, hardware UART SPI and I2C, timers and PWM galore - just enough for most simple projects. When we need to go small, we use a Pro Trinket 3V or 5V, but when size isn't as much of a concern, and an USB-serial converter is required, we reach for an Adafruit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
  Relay 5v DPDT: 5v DPDT Relay, 8 pin
